// Logisim project CPU-2014-Proj.circ as structural Verilog: 5 circuits, main circuit main
module main (
  input  [1:0] phase,
  output [7:0] address,
  output [1:0] out_3,
  output [7:0] r0,
  output [7:0] r1,
  output [7:0] r2,
  output [7:0] datain,
  output [7:0] r3,
  output [7:0] dbus,
  output [7:0] aluout,
  output [7:0] dval,
  output [7:0] sbus,
  output [1:0] aluop,
  output pcsel,
  output pcload
);

  wire clock, dwrite, imload, irload, readwrite, register_2_negative, register_2_zero;
  wire [1:0] dregsel, regsel, sregsel;
  wire [7:0] Immediate_q, Instruction_Register_q, multiplexer_3_out, pc_adder_1_pc_out, register_1_q;

  RAM #(.bus("separate")) ram_1 (
    .addr(address), .din(dbus), .data(datain), .str(readwrite), .clk(clock));  // open: sel, ld, clr
  Clock clock_1 (.out(clock));
  Multiplexer #(.select(2), .width(8), .enable("false")) multiplexer_1 (
    .in0(register_1_q), .in1(Immediate_q), .in2(sbus), .in3(dbus), .out(address), .sel(out_3));
  Register_part Immediate (.D(datain), .en(imload), .Q(Immediate_q), .clk(clock));  // open: clr
  Register_part Instruction_Register (.D(datain), .en(irload), .Q(Instruction_Register_q), .clk(clock));  // open: clr
  Decoder Decoder (
    .irvalue(Instruction_Register_q), .zero(register_2_zero), .negative(register_2_negative), .phase(phase),
    .dregsel(dregsel), .sregsel(sregsel), .aluop(aluop), .pcload(pcsel), .imload(imload), .pcsel(pcload),
    .irload(irload), .readwrite(readwrite), .regsel(regsel), .dwrite(dwrite), .addrsel(out_3));
  Multiplexer #(.select(2), .width(8), .enable("false")) multiplexer_2 (
    .in0(Immediate_q), .in1(sbus), .in2(datain), .in3(aluout), .out(dval), .sel(regsel));
  Multiplexer #(.width(8), .enable("false")) multiplexer_3 (
    .in0(Immediate_q), .in1(pc_adder_1_pc_out), .out(multiplexer_3_out), .sel(pcsel));
  Register_part register_1 (.D(multiplexer_3_out), .en(pcload), .Q(register_1_q), .clk(clock));  // open: clr
  PC_Adder pc_adder_1 (.PC_in(register_1_q), .PC_out(pc_adder_1_pc_out));
  Register register_2 (
    .dwrite(dwrite), .dval(dval), .r0(r0), .r1(r1), .r2(r2), .r3(r3), .dregsel(dregsel), .sregsel(sregsel),
    .dbus(dbus), .zero(register_2_zero), .Negative(register_2_negative), .sbus(sbus));
  ALU ALU (.A(dbus), .B(sbus), .OP(aluop), .Result(aluout));

  // Other names for the same wires on the sheet: addrsel[1:0] = out_3

  // Notes on the sheet:
  //   Register Output
endmodule

module ALU (
  input  [7:0] A,
  input  [7:0] B,
  input  [1:0] OP,
  output [7:0] Result
);

  wire [7:0] adder_1_out, and_1_out, or_1_out, subtractor_1_out, undriven;

  assign and_1_out = A & B & undriven;  // AND_Gate and_1, 8 bits wide
  assign or_1_out = undriven | A | B;  // OR_Gate or_1, 8 bits wide
  Adder adder_1 (.a(A), .b(B), .out(adder_1_out));  // open: cin, cout
  Subtractor subtractor_1 (.a(A), .b(B), .out(subtractor_1_out));  // open: bin, bout
  Multiplexer #(.select(2), .width(8), .enable("false")) multiplexer_1 (
    .in0(and_1_out), .in1(or_1_out), .in2(adder_1_out), .in3(subtractor_1_out), .out(Result), .sel(OP));
endmodule

module Decoder (
  input  [7:0] irvalue,
  input  zero,
  input  negative,
  output [1:0] phase,
  output [1:0] dregsel,
  output [1:0] sregsel,
  output [1:0] aluop,
  output pcload,
  output imload,
  output pcsel,
  output irload,
  output readwrite,
  output [1:0] regsel,
  output dwrite,
  output [1:0] addrsel
);

  wire and_1_out, and_2_out, and_3_out, and_4_out, and_5_out, clock, multiplexer_7_out, multiplexer_9_out,
       not_1_out, not_2_out, not_3_out, not_4_out, or_1_out;
  wire [1:0] multiplexer_4_out, multiplexer_10_out;

  and and_1 (and_1_out, irvalue[4], not_1_out, irvalue[7]);
  not not_1 (not_1_out, irvalue[7]);
  Multiplexer #(.select(2), .enable("false")) multiplexer_1 (
    .in0(1'b1), .in1(1'b0), .in2(1'b0), .in3(1'b0), .out(irload), .sel(phase));
  Multiplexer #(.select(2), .enable("false")) multiplexer_2 (
    .in0(1'b0), .in1(1'b0), .in2(and_1_out), .in3(1'b0), .out(readwrite), .sel(phase));
  Multiplexer #(.select(2), .enable("false")) multiplexer_3 (
    .in0(1'b0), .in1(irvalue[7]), .in2(1'b0), .in3(1'b0), .out(imload), .sel(phase));
  Multiplexer #(.select(4), .width(2), .enable("false")) multiplexer_4 (
    .in0(2'b11), .in1(2'b11), .in2(2'b11), .in3(2'b11), .in4(2'b10), .in5(2'b01), .in6(2'b01), .in7(2'b01),
    .in8(2'b01), .in9(2'b01), .in10(2'b01), .in11(2'b01), .in12(2'b10), .in13(2'b01), .in14(2'b01),
    .in15(2'b00), .out(multiplexer_4_out), .sel({irvalue[4], {3{irvalue[7]}}}));
  Multiplexer #(.select(2), .width(2), .enable("false")) multiplexer_5 (
    .in0(2'b00), .in1(2'b00), .in2(multiplexer_4_out), .in3(2'b00), .out(regsel), .sel(phase));
  Multiplexer #(.select(2), .enable("false")) multiplexer_6 (
    .in0(1'b1), .in1(1'b1), .in2(1'b0), .in3(1'b0), .out(pcsel), .sel(phase));
  Register_part #(.width(2)) register_1 (.Q(phase), .clk(clock), .clr(and_2_out));  // open: D, en
  and and_2 (and_2_out, phase[1], phase[0]);
  Multiplexer #(.select(4), .enable("false")) multiplexer_7 (
    .in0(1'b1), .in1(1'b1), .in2(1'b1), .in3(1'b1), .in4(1'b1), .in5(1'b0), .in6(1'b1), .in7(1'b0),
    .in8(1'b0), .in9(1'b0), .in10(1'b0), .in11(1'b0), .in12(1'b1), .in13(1'b0), .in14(1'b1), .in15(1'b0),
    .out(multiplexer_7_out), .sel({irvalue[4], {3{irvalue[7]}}}));
  not not_2 (not_2_out, zero);
  not not_3 (not_3_out, negative);
  Multiplexer #(.select(2), .enable("false")) multiplexer_8 (
    .in0(1'b0), .in1(1'b0), .in2(multiplexer_7_out), .in3(1'b0), .out(dwrite), .sel(phase));
  and and_3 (and_3_out, not_2_out, not_3_out);
  not not_4 (not_4_out, irvalue[7]);
  Multiplexer #(.select(2), .enable("false")) multiplexer_9 (
    .in0(zero), .in1(not_2_out), .in2(and_3_out), .in3(negative), .out(multiplexer_9_out),
    .sel({irvalue[7], irvalue[4]}));
  and and_4 (and_4_out, not_4_out, irvalue[7], multiplexer_9_out);
  and and_5 (and_5_out, irvalue[4], irvalue[7], irvalue[7], irvalue[7]);
  Multiplexer #(.select(4), .width(2), .enable("false")) multiplexer_10 (
    .in0(2'b00), .in1(2'b00), .in2(2'b00), .in3(2'b00), .in4(2'b10), .in5(2'b10), .in6(2'b00), .in7(2'b00),
    .in8(2'b00), .in9(2'b00), .in10(2'b00), .in11(2'b00), .in12(2'b00), .in13(2'b01), .in14(2'b01),
    .in15(2'b00), .out(multiplexer_10_out), .sel({irvalue[4], {3{irvalue[7]}}}));
  or or_1 (or_1_out, and_4_out, and_5_out);
  Multiplexer #(.select(2), .width(2), .enable("false")) multiplexer_11 (
    .in0(2'b00), .in1(2'b00), .in2(multiplexer_10_out), .in3(2'b00), .out(addrsel), .sel(phase));
  Multiplexer #(.select(2), .enable("false")) multiplexer_12 (
    .in0(1'b1), .in1(irvalue[7]), .in2(or_1_out), .in3(1'b0), .out(pcload), .sel(phase));

  assign aluop = {irvalue[7], irvalue[4]};
  assign dregsel = irvalue[3:2];
  assign {irvalue[6:5], irvalue[0]} = {3{irvalue[7]}};
  assign sregsel = {irvalue[1], irvalue[7]};

  // Other names for the same wires on the sheet: irbit5 = irvalue[7]; irbit6 = irvalue[7]; irbit7 = irvalue[7];
  //   op1[1:0] = {2{irvalue[7]}}; op1op2[3:0] = {irvalue[4], {3{irvalue[7]}}}; op2[1:0] = {irvalue[7], irvalue[4]};
  //   Rs[1:0] = {irvalue[1], irvalue[7]}; irbit4 = irvalue[4]; Rd[1:0] = irvalue[3:2]

  // Notes on the sheet:
  //   Read/Write
  //   IR Load
  //   Decode Logic
  //   Immediate Load
  //   Register Select
  //   PC Select
  //   Phase Counter
  //   Destination Register Write
  //   Address Select
  //   PC Load
endmodule

module Register (
  input  dwrite,
  input  [1:0] dregsel,
  input  [7:0] dval,
  input  [1:0] sregsel,
  output [7:0] r0,
  output [7:0] dbus,
  output [7:0] r1,
  output zero,
  output [7:0] r2,
  output Negative,
  output [7:0] sbus,
  output [7:0] r3
);

  wire clock, demultiplexer_1_out0, demultiplexer_1_out1, demultiplexer_1_out2, demultiplexer_1_out3,
       or_1_out;

  Demultiplexer #(.select(2), .enable("false")) demultiplexer_1 (
    .out0(demultiplexer_1_out0), .out1(demultiplexer_1_out1), .out2(demultiplexer_1_out2),
    .out3(demultiplexer_1_out3), .in(dwrite), .sel(dregsel));
  Register_part register_1 (.D(dval), .en(demultiplexer_1_out0), .Q(r0), .clk(clock));  // open: clr
  Register_part register_2 (.D(dval), .en(demultiplexer_1_out1), .Q(r1), .clk(clock));  // open: clr
  Register_part register_3 (.D(dval), .en(demultiplexer_1_out2), .Q(r2), .clk(clock));  // open: clr
  Register_part register_4 (.D(dval), .en(demultiplexer_1_out3), .Q(r3), .clk(clock));  // open: clr
  Multiplexer #(.select(2), .width(8), .enable("false")) multiplexer_1 (
    .in0(r0), .in1(r1), .in2(r2), .in3(r3), .out(dbus), .sel(dregsel));
  Multiplexer #(.select(2), .width(8), .enable("false")) multiplexer_2 (
    .in0(r0), .in1(r1), .in2(r2), .in3(r3), .out(sbus), .sel(sregsel));
  or or_1 (or_1_out, dbus[0], dbus[1], dbus[2], dbus[3], dbus[4], dbus[5], dbus[6], dbus[7]);
  not not_1 (zero, or_1_out);

  assign Negative = dbus[7];

  // Other names for the same wires on the sheet: drs[1:0] = dregsel
endmodule

module PC_Adder (
  input  [7:0] PC_in,
  output [7:0] PC_out
);

  Adder adder_1 (.a(PC_in), .b(8'h1), .out(PC_out), .cin(1'b0));  // open: cout
endmodule
